# Fritzing sketch DisplayPrototypeSketch (saved by Fritzing 0.9.6b)
breadboards: 1

parts:
  J1 = Hirose FH12-40S-0.5SH [package=SMT]
  Part1 = Adafruit ESP32-S3 Feather [part_number="Adafruit #5323"]
  VCC1 = Battery block 9V
  R1 = Resistor [tolerance=±5% power=0.25 resistance=220 package=THT]

nets:
  N1: J1.pin1, J1.pin5, J1.pin14, J1.pin16, J1.Pin_35, J1.Pin_39, Part1.GND, Part1.A2, VCC1.-
  N2: J1.pin2, J1.pin3, J1.pin4, J1.Pin_38, Part1.3.3V
  N3: J1.pin6, Part1.A3
  N4: J1.pin7, Part1.A4
  N5: J1.pin8, Part1.SCK
  N6: J1.pin9, Part1.A5
  N7: J1.pin17, Part1.MOSI
  N8: J1.Pin_37, Part1.MISO
  N9: J1.Pin_40, R1.Pin_0
  N10: VCC1.+, R1.Pin_1

notes:
  Ground Connections
  This design uses a 4-wire SPI interface to talk to the display. It uses A4 as the chip select pin.
  34 Jumpers are required to attach the display.
  220 Ohm Resistor for Display Backlight Power

custom parts:
  Hirose FH12-40S-0.5SH: FH12-40S-0.5SH SMD FPC connector 20 pin
  Adafruit ESP32-S3 Feather: The ESP32-S3 has arrived in Feather format - and what a great way to get started with this powerful new chip from Espressif! With dual 240 MHz cores, WiFi and BLE support, and native USB, this Feather is great for powering your IoT projects. That's right - it's the new Adafruit ESP32-S3 Feather! With native USB and 8 MB flash, this board will let you upgrade your existing ESP32 projects.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
  Battery block 9V: 9 Volt battery block with 200mil pcb footprint spacing
